# Fritzing sketch wifi-clock-1 (saved by Fritzing 0.9.3b)
circuit board: 9.8cm x 3.5cm
breadboards: 2

parts:
  R2 = Photocell (LDR) [package=THT]
  R3 = Resistor [tolerance=±5% resistance=10k package=THT]
  U1 = MAX7219 [package=dil24]
  R1 = Resistor [tolerance=±5% resistance=10k package=THT]
  WeMosD1 = WeMos D1 Mini
  S1 = Pushbutton 90deg
  S2 = Pushbutton 90deg
  U3 = 7-SEGMENT-DISPLAY [package=7-segment-display]
  U2 = 7-SEGMENT-DISPLAY [package=7-segment-display]
  U5 = 7-SEGMENT-DISPLAY [package=7-segment-display]
  U4 = 7-SEGMENT-DISPLAY [package=7-segment-display]

nets:
  N1: R2.pin_0, R3.Pin_1, WeMosD1.A0
  GND: R2.pin_1, U1.GND, U1.GND2, WeMosD1.G, S2.Pin_2
  N2: R3.Pin_0, WeMosD1.3V3, S1.Pin_1
  N3: U1.DIN, WeMosD1.D1
  dig0: U1.DIG0, U2.G2
  dig2: U1.DIG2, U4.G1
  dig3: U1.DIG3, U5.G1
  dig1: U1.DIG1, U3.G2
  d2: U1.LOAD, WeMosD1.D2
  d0: U1.CLK, WeMosD1.D0
  a: U1.SEGA, U3.A, U2.A, U5.A, U4.D
  f: U1.SEGF, U3.F, U2.F, U5.F, U4.C
  b: U1.SEGB, U3.B, U2.B, U5.B, U4.E
  g: U1.SEGG, U3.G, U2.G, U5.G, U4.G
  N4: U1.ISET, R1.Pin_0
  5V: U1.VCC, R1.Pin_1, WeMosD1.5V
  c: U1.SEGC, U3.C, U2.C, U5.C, U4.F
  e: U1.SEGE, U3.E, U2.E, U5.E, U4.B
  DP: U1.SEGDP, U3.DP, U4.DP
  d: U1.SEGD, U3.D, U2.D, U5.D, U4.A
  N5: WeMosD1.D4, S2.Pin_1
  N6: WeMosD1.D8, S1.Pin_2
